// Digital circuit Control Unit.dig as structural Verilog
module Control_Unit (
  input  [15:0] IR,
  input  CLK,
  input  S,
  input  R,
  input  I,
  input  IEN,
  input  FGI,
  input  FGO,
  input  E,
  input  [15:0] AC,
  input  [15:0] DR,
  input  C_OUT,
  output [6:0] BUS_CONTROL,
  output S_CLR,
  output I_LD,
  output I_D,
  output R_J,
  output R_K,
  output IEN_J,
  output IEN_K,
  output FGI_K,
  output FGO_K,
  output AR_LD,
  output AR_INR,
  output AR_CLR,
  output MEM_read,
  output MEM_write,
  output PC_LD,
  output PC_INCR,
  output PC_CLR,
  output DR_LD,
  output DR_INCR,
  output AC_LD,
  output AC_INCR,
  output AC_CLR,
  output [6:0] AL_OP,
  output OUTR_LD,
  output IR_LD,
  output TR_LD,
  output [15:0] T,
  output [7:0] D,
  output E_J,
  output E_K
);

  wire and_3_out, and_4_out, and_5_out, and_6_out, and_7_out, and_8_out, and_9_out, and_10_out, and_11_out,
       and_12_out, and_13_out, and_14_out, and_15_out, and_16_out, and_20_out, and_21_out, and_22_out,
       and_23_out, and_24_out, and_25_out, and_26_out, and_27_out, and_30_out, and_31_out, and_33_out,
       and_34_out, and_35_out, and_36_out, and_37_out, and_38_out, and_39_out, and_40_out, and_41_out,
       and_42_out, and_43_out, and_44_out, and_45_out, and_46_out, and_47_out, and_48_out, and_49_out,
       and_53_out, and_54_out, and_55_out, and_56_out, and_57_out, and_58_out, and_59_out, and_60_out,
       nor_1_out, nor_2_out, or_1_out, or_2_out, or_3_out, or_4_out, or_5_out, or_6_out, or_7_out, or_8_out,
       or_9_out, or_10_out, or_16_out, or_17_out, p, r_t;
  wire [3:0] SC_out;

  and and_1 (r_t, D[7], ~I, T[3]);  // And
  and and_2 (p, D[7], I, T[3]);
  Decoder #(.Selector_Bits(3)) decoder_1 (
    .sel(IR[14:12]), .out_0(D[0]), .out_1(D[1]), .out_2(D[2]), .out_3(D[3]), .out_4(D[4]), .out_5(D[5]),
    .out_6(D[6]), .out_7(D[7]));
  or or_1 (or_1_out, D[0], D[1], D[2], D[5]);
  or or_2 (or_2_out, D[3], D[4]);
  and and_3 (and_3_out, R, T[2]);
  and and_4 (and_4_out, T[5], or_1_out);
  and and_5 (and_5_out, T[4], or_2_out);
  and and_6 (and_6_out, T[6], D[6]);
  and and_7 (and_7_out, T[3], D[7]);
  or or_3 (or_3_out, and_3_out, and_4_out, and_5_out, and_6_out, and_7_out);
  Counter #(.Bits(4)) SC (.en(S), .C(CLK), .clr(or_3_out), .out(SC_out));  // open: ovf
  nor nor_1 (nor_1_out, DR[0], DR[1], DR[2], DR[3], DR[4], DR[5], DR[6], DR[7], DR[8], DR[9], DR[10], DR[11], DR[12], DR[13], DR[14], DR[15]);
  Decoder #(.Selector_Bits(4)) decoder_2 (
    .sel(SC_out), .out_0(T[0]), .out_1(T[1]), .out_2(T[2]), .out_3(T[3]), .out_4(T[4]), .out_5(T[5]),
    .out_6(T[6]), .out_7(T[7]), .out_8(T[8]), .out_9(T[9]), .out_10(T[10]), .out_11(T[11]), .out_12(T[12]),
    .out_13(T[13]), .out_14(T[14]), .out_15(T[15]));
  nor nor_2 (nor_2_out, AC[0], AC[1], AC[2], AC[3], AC[4], AC[5], AC[6], AC[7], AC[8], AC[9], AC[10], AC[11], AC[12], AC[13], AC[14], AC[15]);
  and and_8 (and_8_out, IR[2], nor_2_out);
  and and_9 (and_9_out, r_t, IR[7]);
  and and_10 (and_10_out, r_t, IR[6]);
  and and_11 (and_11_out, ~D[7], I, T[3]);  // And
  or or_4 (or_4_out, D[0], D[1], D[2], D[6]);
  and and_12 (and_12_out, IR[1], ~E);  // And
  and and_13 (and_13_out, IR[3], AC[15]);
  and and_14 (and_14_out, IR[4], ~AC[15]);  // And
  and and_15 (and_15_out, IR[9], FGI);
  and and_16 (and_16_out, IR[8], FGO);
  or or_5 (or_5_out, T[0], T[2]);
  or or_6 (or_6_out, D[3], D[5]);
  or or_7 (or_7_out, and_12_out, and_13_out, and_8_out, and_14_out);
  or or_8 (or_8_out, and_15_out, and_16_out);
  or or_9 (or_9_out, D[0], D[1], D[2]);
  or or_10 (or_10_out, IR[9], IR[7], IR[6]);
  and and_17 (AL_OP[1], D[1], T[5]);
  and and_18 (AL_OP[3], p, IR[11]);
  and and_19 (AL_OP[5], r_t, IR[7]);
  and and_20 (and_20_out, D[1], T[5]);
  and and_21 (and_21_out, D[4], T[4]);
  and and_22 (and_22_out, D[5], T[5]);
  and and_23 (and_23_out, D[5], T[4]);
  and and_24 (and_24_out, D[2], T[5]);
  and and_25 (and_25_out, D[6], T[6]);
  and and_26 (and_26_out, D[3], T[4]);
  and and_27 (and_27_out, p, IR[10]);
  and and_28 (BUS_CONTROL[4], ~R, T[2]);  // And
  and and_29 (BUS_CONTROL[5], R, T[1]);
  and and_30 (and_30_out, ~R, T[1]);  // And
  and and_31 (and_31_out, T[4], or_4_out);
  and and_32 (AL_OP[6], r_t, IR[6]);
  or or_11 (BUS_CONTROL[0], and_21_out, and_22_out);
  or or_12 (BUS_CONTROL[1], and_23_out, T[0]);
  or or_13 (BUS_CONTROL[2], and_24_out, and_25_out);
  or or_14 (BUS_CONTROL[3], and_26_out, and_27_out);
  or or_15 (BUS_CONTROL[6], and_30_out, and_11_out, and_31_out);
  or or_16 (or_16_out, FGI, FGO);
  and and_33 (and_33_out, R, T[2]);
  and and_34 (and_34_out, p, IR[6]);
  and and_35 (and_35_out, ~D[7], I, T[3]);  // And
  and and_36 (and_36_out, ~R, or_5_out);  // And
  and and_37 (and_37_out, R, T[1]);
  and and_38 (and_38_out, D[6], T[6]);
  and and_39 (and_39_out, or_6_out, T[4]);
  and and_40 (and_40_out, D[4], T[4]);
  and and_41 (and_41_out, D[5], T[5]);
  and and_42 (and_42_out, ~R, T[1]);  // And
  and and_43 (and_43_out, R, T[2]);
  and and_44 (and_44_out, D[6], T[6], nor_1_out);
  and and_45 (and_45_out, r_t, or_7_out);
  and and_46 (and_46_out, p, or_8_out);
  or or_17 (or_17_out, D[0], D[1], D[2], D[6]);
  and and_47 (and_47_out, or_9_out, T[5]);
  and and_48 (and_48_out, or_10_out, r_t);
  and and_49 (and_49_out, p, IR[11]);
  and and_50 (AL_OP[0], D[0], T[5]);
  and and_51 (AL_OP[2], D[2], T[5]);
  and and_52 (AL_OP[4], r_t, IR[9]);
  and and_53 (and_53_out, AC[15], and_10_out);
  and and_54 (and_54_out, AC[0], and_9_out);
  and and_55 (and_55_out, C_OUT, and_20_out);
  and and_56 (and_56_out, r_t, IR[8]);
  and and_57 (and_57_out, and_20_out, ~C_OUT);  // And
  and and_58 (and_58_out, and_9_out, ~AC[0]);  // And
  and and_59 (and_59_out, and_10_out, ~AC[15]);  // And
  and and_60 (and_60_out, r_t, IR[10]);
  and and_61 (S_CLR, r_t, IR[0]);
  and and_62 (I_LD, ~r_t, T[2]);  // And
  and and_63 (R_J, ~T[0], ~T[1], ~T[2], IEN, or_16_out);  // And
  and and_64 (R_K, R, T[2]);
  and and_65 (IEN_J, p, IR[7]);
  or or_18 (IEN_K, and_33_out, and_34_out);
  and and_66 (FGI_K, p, IR[11]);
  and and_67 (FGO_K, p, IR[10]);
  or or_19 (AR_LD, and_35_out, and_36_out);
  and and_68 (AR_INR, D[5], T[4]);
  and and_69 (AR_CLR, R, T[0]);
  or or_20 (MEM_write, and_37_out, and_38_out, and_39_out);
  or or_21 (PC_LD, and_40_out, and_41_out);
  or or_22 (PC_INCR, and_42_out, and_43_out, and_44_out, and_45_out, and_46_out);
  and and_70 (PC_CLR, R, T[1]);
  and and_71 (DR_LD, or_17_out, T[4]);
  and and_72 (DR_INCR, D[6], T[5]);
  or or_23 (AC_LD, and_47_out, and_48_out, and_49_out);
  and and_73 (AC_INCR, r_t, IR[5]);
  and and_74 (AC_CLR, r_t, IR[11]);
  and and_75 (OUTR_LD, p, IR[10]);
  and and_76 (IR_LD, ~R, T[1]);  // And
  and and_77 (TR_LD, R, T[0]);
  or or_24 (E_J, and_53_out, and_54_out, and_55_out, and_56_out);
  or or_25 (E_K, and_56_out, and_57_out, and_58_out, and_59_out, and_60_out);

  assign I_D = IR[15];
  assign MEM_read = 1'b1;

  // Other names for the same wires on the sheet: AC_0 = AC[0]; AC_15 = AC[15]; D_0 = D[0]; D_1 = D[1]; D_2 = D[2];
  //   D_3 = D[3]; D_4 = D[4]; D_5 = D[5]; D_6 = D[6]; D_7 = D[7]; B0 = IR[0]; B1 = IR[1]; B2 = IR[2]; B3 = IR[3];
  //   B4 = IR[4]; B5 = IR[5]; B6 = IR[6]; B7 = IR[7]; B8 = IR[8]; B9 = IR[9]; B10 = IR[10]; B11 = IR[11]; T_0 = T[0];
  //   T_1 = T[1]; T_2 = T[2]; T_3 = T[3]; T_4 = T[4]; T_5 = T[5]; T_6 = T[6]; T_7 = T[7]; T_8 = T[8]; T_9 = T[9];
  //   T_10 = T[10]; T_11 = T[11]; T_12 = T[12]; T_13 = T[13]; T_14 = T[14]; T_15 = T[15]
endmodule
