// Digital circuit Full Picture v1.dig as structural Verilog
module Full_Picture_v1 (
  input  CLK,
  input  [7:0] INPUT,
  input  INPR_LD,
  input  [11:0] PC_Target,
  input  [1:0] SelectBreakMethod,
  output [7:0] OUTPUT
);

  wire AC_CLR, AC_INCR, AC_LD, and_2_out, AR_CLR, AR_INR, AR_LD, BlankAddr, C_OUT, CLK_t, comparator_1_eq,
       D1A, D1B, D1C, D1D, D2A, D2B, D2C, D2D, D3A, D3B, D3C, D3D, DR_INCR, DR_LD, E, E_J, E_K,
       Empty_Output_Buffer_out, FGI, FGI_K, FGO, FGO_K, I, I_D, I_LD, IEN, IEN_J, IEN_K, Indirect,
       Input_Available_out, INPUT_CLK_out, IR_LD, MEM_read, MEM_write, MemRef, multiplexer_1_out, not_1_out,
       OUTR_LD, PC_CLR, PC_INCR, PC_LD, R, R_J, R_K, reset_1_out, S, S_CLR, SS1A, SS1B, SS1C, SS1D, SS1E,
       SS1F, SS1G, SS2A, SS2B, SS2C, SS2D, SS2E, SS2F, SS2G, SS3A, SS3B, SS3C, SS3D, SS3E, SS3F, SS3G,
       T_Fetch, TR_LD, x_1, x_2, x_3, x_4, x_5, x_6, x_7;
  wire [6:0] AL_OP;
  wire [7:0] D, INPR;
  wire [11:0] AR, PC;
  wire [15:0] AC, ALU_OUT, Bus, DR, IR, Letter1, Letter1_blankable, Letter2, Letter2_blankable, Letter3,
       Letter3_blankable, MEM_d, T, TR;

  Button Input_Available (.out(Input_Available_out));
  Button Empty_Output_Buffer (.out(Empty_Output_Buffer_out));
  Reset #(.invertOutput("false")) reset_1 (.out(reset_1_out));
  JK_FF_AS u_S (.Set(reset_1_out), .J(1'b0), .C(CLK_t), .K(S_CLR), .Clr(1'b0), .Q(S));  // open: nQ
  JK_FF u_R (.J(R_J), .C(CLK_t), .K(R_K), .Q(R));  // open: nQ
  // I I: pin names not known; wires that end beside it: CLK_t, I_LD, I_D, I
  JK_FF u_IEN (.J(IEN_J), .C(CLK_t), .K(IEN_K), .Q(IEN));  // open: nQ
  JK_FF_AS u_FGI (.Set(Input_Available_out), .J(1'b0), .C(CLK_t), .K(FGI_K), .Clr(1'b0), .Q(FGI));  // open: nQ
  JK_FF_AS u_FGO (.Set(Empty_Output_Buffer_out), .J(1'b0), .C(CLK_t), .K(FGO_K), .Clr(1'b0), .Q(FGO));  // open: nQ
  LED START (.in(S));
  // Adder_and_Logic_Circuit adder_and_logic_circuit_1: pin names not known; wires that end beside it: AC, DR, INPR, AL_OP, E, ALU_OUT, C_OUT
  JK_FF u_E (.J(E_J), .C(CLK_t), .K(E_K), .Q(E));  // open: nQ
  Button INPUT_CLK (.out(INPUT_CLK_out));
  // PC PC: pin names not known; wires that end beside it: PC_CLR, Bus[11:0], PC_LD, PC_INCR, CLK_t, PC
  // Probe on AR
  RAMDualPort #(.AddrBits(12), .isProgramMemory("true"), .Bits(16)) MEM (
    .A(AR), .Din(Bus), .str(MEM_write), .C(CLK_t), .ld(MEM_read), .D(MEM_d));
  CounterPreset #(.Bits(12)) u_AR (
    .en(AR_INR), .C(CLK_t), .dir(1'b0), .in(Bus[11:0]), .ld(AR_LD), .clr(AR_CLR), .out(AR));  // open: ovf
  CounterPreset #(.Bits(16)) u_DR (
    .en(DR_INCR), .C(CLK_t), .dir(1'b0), .in(Bus), .ld(DR_LD), .clr(1'b0), .out(DR));  // open: ovf
  CounterPreset #(.Bits(16)) u_AC (
    .en(AC_INCR), .C(CLK_t), .dir(1'b0), .in(ALU_OUT), .ld(AC_LD), .clr(AC_CLR), .out(AC));  // open: ovf
  CounterPreset #(.Bits(8)) u_INPR (
    .en(1'b0), .C(INPUT_CLK_out), .dir(1'b0), .in(INPUT), .ld(INPR_LD), .clr(1'b0), .out(INPR));  // open: ovf
  CounterPreset #(.Bits(16)) u_IR (
    .en(1'b0), .C(CLK_t), .dir(1'b0), .in(Bus), .ld(IR_LD), .clr(1'b0), .out(IR));  // open: ovf
  CounterPreset #(.Bits(16)) u_TR (
    .en(1'b0), .C(CLK_t), .dir(1'b0), .in(Bus), .ld(TR_LD), .clr(1'b0), .out(TR));  // open: ovf
  CounterPreset #(.Bits(8)) OUTR (
    .en(1'b0), .C(CLK_t), .dir(1'b0), .in(Bus[7:0]), .ld(OUTR_LD), .clr(1'b0), .out(OUTPUT));  // open: ovf
  // Probe on AR
  assign Bus = x_7 ? MEM_d : 16'bz;  // Driver driver_1
  assign Bus = x_1 ? {4'b0000, AR} : 16'bz;  // Driver driver_2
  assign Bus = x_2 ? {4'b0000, PC} : 16'bz;  // Driver driver_3
  assign Bus = x_3 ? DR : 16'bz;  // Driver driver_4
  assign Bus = x_4 ? AC : 16'bz;  // Driver driver_5
  assign Bus = x_5 ? IR : 16'bz;  // Driver driver_6
  assign Bus = x_6 ? TR : 16'bz;  // Driver driver_7
  // Probe on Bus
  Control_Unit control_unit_1 (
    .IR(IR), .CLK(CLK_t), .S(S), .R(R), .I(I), .IEN(IEN), .FGI(FGI), .FGO(FGO), .E(E), .AC(AC), .DR(DR),
    .C_OUT(C_OUT), .BUS_CONTROL({x_7, x_6, x_5, x_4, x_3, x_2, x_1}), .S_CLR(S_CLR), .I_LD(I_LD), .I_D(I_D),
    .R_J(R_J), .R_K(R_K), .IEN_J(IEN_J), .IEN_K(IEN_K), .FGI_K(FGI_K), .FGO_K(FGO_K), .AR_LD(AR_LD),
    .AR_INR(AR_INR), .AR_CLR(AR_CLR), .MEM_read(MEM_read), .MEM_write(MEM_write), .PC_LD(PC_LD),
    .PC_INCR(PC_INCR), .PC_CLR(PC_CLR), .DR_LD(DR_LD), .DR_INCR(DR_INCR), .AC_LD(AC_LD), .AC_INCR(AC_INCR),
    .AC_CLR(AC_CLR), .AL_OP(AL_OP), .OUTR_LD(OUTR_LD), .IR_LD(IR_LD), .TR_LD(TR_LD), .T(T), .D(D), .E_J(E_J),
    .E_K(E_K));
  and and_1 (CLK_t, CLK, 1'b1);
  Seven_Seg seven_seg_1 (.a(1'b0), .b(and_2_out), .c(and_2_out), .d(1'b0), .e(1'b0), .f(1'b0), .g(1'b0), .dp(1'b0));
  and and_2 (and_2_out, T_Fetch, Indirect);
  Seven_Seg_Hex seven_seg_hex_1 (.d(PC[7:4]), .dp(1'b0));
  Seven_Seg_Hex seven_seg_hex_2 (.d(PC[11:8]), .dp(1'b0));
  Seven_Seg_Hex seven_seg_hex_3 (.d(AC[11:8]), .dp(1'b0));
  Seven_Seg_Hex seven_seg_hex_4 (.d(AC[15:12]), .dp(1'b0));
  Seven_Seg_Hex seven_seg_hex_5 (.d(IR[11:8]), .dp(1'b0));
  Seven_Seg_Hex seven_seg_hex_6 (.d(IR[15:12]), .dp(1'b0));
  Seven_Seg_Hex seven_seg_hex_7 (.d(INPR[3:0]), .dp(1'b0));
  Seven_Seg_Hex seven_seg_hex_8 (.d(INPR[7:4]), .dp(1'b0));
  SixteenSeg sixteenseg_1 (.led(Letter3_blankable), .dp(1'b0));
  Seven_Seg_Hex seven_seg_hex_9 (.d(PC[3:0]), .dp(1'b0));
  Seven_Seg_Hex seven_seg_hex_10 (.d(AC[3:0]), .dp(1'b0));
  Seven_Seg_Hex seven_seg_hex_11 (.d(AC[7:4]), .dp(1'b0));
  Seven_Seg_Hex seven_seg_hex_12 (.d(IR[3:0]), .dp(1'b0));
  Seven_Seg_Hex seven_seg_hex_13 (.d(IR[7:4]), .dp(1'b0));
  SixteenSeg sixteenseg_2 (.led(Letter2_blankable), .dp(1'b0));
  SixteenSeg sixteenseg_3 (.led(Letter1_blankable), .dp(1'b0));
  Seven_Seg_Hex seven_seg_hex_14 (.d(AR[11:8]), .dp(1'b0));
  Seven_Seg_Hex seven_seg_hex_15 (.d(DR[15:12]), .dp(1'b0));
  Seven_Seg_Hex seven_seg_hex_16 (.d(TR[15:12]), .dp(1'b0));
  Seven_Seg seven_seg_2 (.a(SS1A), .b(SS1B), .c(SS1C), .d(SS1D), .e(SS1E), .f(SS1F), .g(SS1G), .dp(1'b0));
  Seven_Seg_Hex seven_seg_hex_17 (.d(AR[3:0]), .dp(1'b0));
  Seven_Seg_Hex seven_seg_hex_18 (.d(AR[7:4]), .dp(1'b0));
  Seven_Seg_Hex seven_seg_hex_19 (.d(DR[7:4]), .dp(1'b0));
  Seven_Seg_Hex seven_seg_hex_20 (.d(DR[11:8]), .dp(1'b0));
  Seven_Seg_Hex seven_seg_hex_21 (.d(TR[7:4]), .dp(1'b0));
  Seven_Seg_Hex seven_seg_hex_22 (.d(TR[11:8]), .dp(1'b0));
  Seven_Seg_Hex seven_seg_hex_23 (.d(OUTPUT[3:0]), .dp(1'b0));
  Seven_Seg_Hex seven_seg_hex_24 (.d(OUTPUT[7:4]), .dp(1'b0));
  Seven_Seg seven_seg_3 (.a(SS2A), .b(SS2B), .c(SS2C), .d(SS2D), .e(SS2E), .f(SS2F), .g(SS2G), .dp(1'b0));
  Seven_Seg_Hex seven_seg_hex_25 (.d(DR[3:0]), .dp(1'b0));
  Seven_Seg_Hex seven_seg_hex_26 (.d(TR[3:0]), .dp(1'b0));
  Seven_Seg seven_seg_4 (.a(SS3A), .b(SS3B), .c(SS3C), .d(SS3D), .e(SS3E), .f(SS3F), .g(SS3G), .dp(1'b0));
  LED START_2 (.in(S));
  LED I_FLAG (.in(I));
  LED E_FLAG (.in(E));
  LED R_FLAG (.in(R));
  LED IEN_FLAG (.in(IEN));
  LED FGI_FLAG (.in(FGI));
  LED FGO_FLAG (.in(FGO));
  LED T0 (.in(T[0]));
  LED T2 (.in(T[2]));
  LED T4 (.in(T[4]));
  LED T6 (.in(T[6]));
  LED T8 (.in(T[8]));
  LED T10 (.in(T[10]));
  LED T12 (.in(T[12]));
  LED T14 (.in(T[14]));
  LED D_0 (.in(D[0]));
  LED D_2 (.in(D[2]));
  LED D_4 (.in(D[4]));
  LED D_6 (.in(D[6]));
  LED D_1 (.in(D[1]));
  LED D_3 (.in(D[3]));
  LED D_5 (.in(D[5]));
  LED D_7 (.in(D[7]));
  LED T1 (.in(T[1]));
  LED T3 (.in(T[3]));
  LED T5 (.in(T[5]));
  LED T7 (.in(T[7]));
  LED T9 (.in(T[9]));
  LED T11 (.in(T[11]));
  LED T13 (.in(T[13]));
  LED T15 (.in(T[15]));
  not not_1 (not_1_out, S);
  Comparator #(.Bits(12)) comparator_1 (.a(PC), .b(PC_Target), .eq(comparator_1_eq));  // open: gt, lt
  Multiplexer #(.Selector_Bits(2)) multiplexer_1 (
    .sel(SelectBreakMethod), .in_0(not_1_out), .in_1(T[3]), .in_2(comparator_1_eq), .in_3(1'b0),
    .out(multiplexer_1_out));
  Break break_1 (.brk(multiplexer_1_out));
  // AlphanumericInstructionDecoderIC alphanumericinstructiondecoderic_1: pin names not known; wires that end beside it: IR, Letter1, Letter2, Letter3, Indirect, D1A, D1B, D1C, D1D, D2A, D2B, D2C, D2D, D3A, D3B, D3C, D3D, MemRef
  nor nor_1 (T_Fetch, T[0], T[1], T[2]);
  and and_3 (BlankAddr, MemRef, T_Fetch);
  // SevenSegDecoderWithBlank sevensegdecoderwithblank_1: pin names not known; wires that end beside it: BlankAddr, D1A, D1B, D1C, D1D, SS1G, SS1F, SS1E, SS1D, SS1C, SS1B, SS1A
  Multiplexer #(.Bits(16)) multiplexer_2 (.sel(T_Fetch), .in_0({16{1'b0}}), .in_1(Letter1), .out(Letter1_blankable));
  // SevenSegDecoderWithBlank sevensegdecoderwithblank_2: pin names not known; wires that end beside it: BlankAddr, D2A, D2B, D2C, D2D, SS2G, SS2F, SS2E, SS2D, SS2C, SS2B, SS2A
  Multiplexer #(.Bits(16)) multiplexer_3 (.sel(T_Fetch), .in_0({16{1'b0}}), .in_1(Letter2), .out(Letter2_blankable));
  // SevenSegDecoderWithBlank sevensegdecoderwithblank_3: pin names not known; wires that end beside it: BlankAddr, D3A, D3B, D3C, D3D, SS3G, SS3F, SS3E, SS3D, SS3C, SS3B, SS3A
  Multiplexer #(.Bits(16)) multiplexer_4 (.sel(T_Fetch), .in_0({16{1'b0}}), .in_1(Letter3), .out(Letter3_blankable));

  // Other names for the same wires on the sheet: OUTR[7:0] = OUTPUT; T_0 = T[0]; T_1 = T[1]; T_2 = T[2]; T_3 = T[3]

  // Notes on the sheet:
  //   CLK: Hz: 20
  //   THE MANO COMPUTER
  //   DATA PATH
  //   CONTROL UNIT
  //   SYSTEM CLOCK
  //   Bus Control
  //   DISPLAYS, TEST CASES, DEBUG
  //   PC
  //   AC
  //   IR
  //   INPR
  //   AR
  //   DR
  //   TR
  //   OUTR
  //   1: Single instruction
  //   2: Break when PC has a given value
  //   0: Break at HALT
endmodule

/* Test case CLA:
CLK	AC


init S=1;	#Start computer
init AC=0x6363; #Prepare AC
program(0x7800)	#CLA register instruction

repeat(4) C	X
0	0
*/

/* Test case AND_DIRECT:
		CLK	AC

init S=1;	#Start computer
init AC=0x6363; #Prepare AC
program(0x0002, 0, 0x0F0F)	#AND MEM[2] to AC

		0	0x6363		
		repeat(6) C	X
		0	0x0303
*/

/* Test case AND_INDIRECT:
		CLK	AC

init S=1;	#Start computer
init AC=0x6363; #Prepare AC
program(0x8002, 0, 3, 0x0F0F)	#AND MEM[MEM[2]] to AC

		0	0x6363		
repeat(6)	C	X
		0	0x0303
*/

/* Test case INP:
CLK	AC

init INPR=0x63;
init S=1;
program(0xF800)

repeat(3) C	X
C	0x63
*/

/* Test case Interrupt Service Routine:
		CLK	PC	IR	R	IEN	AR	AC	FGO	OUTR	S

#	0	1	2	3	4	5	6	7
#	reservd	BUN	INC	INC	INC	HLT	OUT	BUN
program(0x0000, 0x4006, 0x7020, 0x7020, 0x7020, 0x7001, 0xF400, 0xC000)
init S=1;
init PC=2;
init IEN=1;
init FGO=1;

		0	2	X	0	1	X	X	1	X	1
repeat(40)	C	X	X	X	X	X	X	X	X	X
*/

/* Test case CLE:
		CLK	E

init S=1;	#Start computer
init E=1; 	#Prepare E
program(0x7400)	#CLE register instruction

repeat(4) 	C	X
		0	0
*/

/* Test case OUT:
		CLK	AC	OUTR	FGO

init AC=0x0063;
init S=1;
init FGO=1;
program(0xF400)

		0	0x0063	0	1
repeat(3)	C	X	X	X
		C	X	0x63	0
*/

/* Test case CMA:
		CLK	AC

init S=1;	#Start computer
init AC=0xF0F0;	#Prepare AC
program(0x7200)	#CMA register instruction

repeat(4) 	C	X
		0	0x0F0F
*/

/* Test case ADD_DIRECT:
		CLK	AC

init S=1;	#Start computer
init AC=100; #Prepare AC
program(0x1002, 0, 3)	#ADD MEM[2] to AC

		0	100		
		repeat(6) C	X
		0	103
*/

/* Test case ADD_INDIRECT:
		CLK	AC

init S=1;	#Start computer
init AC=100; #Prepare AC
program(0x9002, 0, 3, 10)	#ADD MEM[MEM[2]] to AC

		0	100		
		repeat(6) C	X
		0	110
*/

/* Test case LDA_DIRECT:
		CLK	AC

init S=1;	#Start computer
init AC=100; 	#Prepare AC
program(0x2002, 0, 3)	#LOAD MEM[2] to AC

		0	100		
repeat(6)	C	X
		0	3
*/

/* Test case LDA_INDIRECT:
		CLK	AC

init S=1;	#Start computer
init AC=100; 	#Prepare AC
program(0xA002, 0, 3, 303)	#LOAD MEM[MEM[2]] to AC

		0	100		
repeat(6)	C	X
		0	303
*/

/* Test case SKI_SKIP:
		CLK	PC	AC	FGI
init AC=1;
init S=1;
program(0xF200, 0x7020, 0x7200)
init FGI=1;

		0	0	1	1
repeat(4)	C	X	X	X
		C	2	X	X
repeat(4)	C	X	X	X
		C	X	0xFFFE	1
*/

/* Test case CME:
		CLK	E

init S=1;		#Start computer
init E=1; 		#Prepare E
program(0x7100, 0x7100)	#CME register instruction (twice)

repeat(4) 	C	X
		0	0
repeat(4) 	C	X
		0	1		
*/

/* Test case SKI_NOSKIP:
		CLK	PC	AC	FGI

init FGI=0;
init AC=1;
init S=1;
program(0xF200, 0x7020, 0x7200)

		0	0	1	0
repeat(4)	C	X	X	X
		C	1	1	X
repeat(4)	C	X	X	X
		C	X	2	0
*/

/* Test case CIR:
		CLK	AC	E

init S=1;		#Start computer
init AC=0x0101;		#Prepare AC
init E=1;
program(0x7080, 0x7080)	#CIR register instruction (twice)

		0	0x0101	1
repeat(4) 	C	X	X
		0	0x8080	1

repeat(4) 	C	X	X
		0	0xC040	0
*/

/* Test case STA_DIRECT:
		CLK	AC	PC

init S=1;	#Start computer
init AC=100; 	#Prepare AC
program(0x3005, 0x7800, 0x2005, 0, 0, 0)	#STORE AC to MEM[5]; CLA; LDA MEM[5] to AC

		0	100	0
repeat(5)	C	X	X
		0	100	1

repeat(4)	C	X	X
		0	0	2

repeat(6)	C	X	X
		0	100	3
*/

/* Test case STA_INDIRECT:
		CLK	AC	PC	SC

init S=1;	#Start computer
init AC=100; 	#Prepare AC
program(0xB005, 0x7800, 0xA005, 0, 0, 4)	#STORE AC to MEM[MEM[5]]; CLA; LDA MEM[MEM[5]] to AC

		0	100	0	X
repeat(5)	C	X	X	X
		0	100	1	X

repeat(4)	C	X	X	X
		0	0	2	X

repeat(6)	C	X	X	X
		0	100	3	X
*/

/* Test case CIL:
		CLK	AC	E

init S=1;		#Start computer
init AC=0x0101;		#Prepare AC
init E=1;
program(0x7040, 0x7040)	#CIL register instruction (twice)

		0	0x0101	1
repeat(4) 	C	X	X
		0	0x0203	0

repeat(4) 	C	X	X
		0	0x0406	0
*/

/* Test case SKO_SKIP:
		CLK	PC	AR	IR	AC	FGO
init AC=1;
init S=1;
program(0xF100, 0x7020, 0x7200)
init FGO=1;

		0	0	X	X	1	1
repeat(4)	C	X	X	X	X	X
		0	2	X	X	X	X
repeat(4)	C	X	X	X	X	X
		0	X	X	X	0xFFFE	1
*/

/* Test case INC:
		CLK	AC

init S=1;		#Start computer
init AC=0x0101;		#Prepare AC

program(0x7020, 0x7020)	#CIL register instruction (twice)

		0	0x0101
repeat(4) 	C	X
		0	0x0102

repeat(4) 	C	X
		0	0x0103
*/

/* Test case BUN_DIRECT:
		CLK	PC	AC

init S=1;	#Start computer
init AC=0;
program(0x4005, 0x7020, 0x7020, 0x7020, 0x7020, 0x7200) #Branch to address 5

		0	0	0
repeat(5)	C	X	X
		0	5	0
*/

/* Test case BUN_INDIRECT:
		CLK	PC	AC

init S=1;	#Start computer
init AC=0;
program(0xC005, 0x7020, 0x7020, 0x7020, 0x7020, 0x0007, 0x7020, 0x7020) #Branch to address at MEM[5]

		0	0	0
repeat(5)	C	X	X
		0	7	0
*/

/* Test case SKO_NOSKIP:
		CLK	PC	AR	IR	AC	FGO
init AC=1;
init S=1;
program(0xF100, 0x7020, 0x7200)
init FGO=0;

		0	0	X	X	1	0
repeat(4)	C	X	X	X	X	X
		0	1	X	X	X	X
repeat(4)	C	X	X	X	X	X
		0	X	X	X	2	0
*/

/* Test case SPA-Skip:
		CLK	AC	PC

init S=1;		#Start computer
init AC=0x0F0F;		#Prepare AC

program(0x7010, 0x7200, 0x7010, 0x7200)	#SPA CMA SPA CMA

		0	0x0F0F	0
repeat(4) 	C	X	X
		0	0x0F0F	2
*/

/* Test case BSA_DIRECT:
		CLK	PC	AC

init S=1;	#Start computer
init AC=0;
#	0	1	2	3	4	5	6	7
program(0x5005, 0x7020, 0x0000, 0x000, 0x0000, 0x0000, 0x7200, 0xC005 ) #Save PC to address 5 and continue execution from 6, then indirect return instruction at 7.

		0	0	0
repeat(6)	C	X	X
		0	6	X
repeat(4)	C	X	X	#CMA instruction at address 6
		0	7	X
repeat(5)	C	X	X	#Indirect BUN instruction at address 7
		0	1	X
repeat(4)	C	X	X	#0x7020 instruction (INC) at address 1
		0	2	0x0000	#
*/

/* Test case BSA_INDIRECT:
		CLK	PC	AC

init S=1;	#Start computer
init AC=0;
#	0	1	2	3	4	5	6	7
program(0xD003, 0x7020, 0x0000, 0x005, 0x0000, 0x0000, 0x7200, 0xC005 ) #Save PC to address found at MEM[3] and continue execution from 6, then indirect return instruction at 7.

		0	0	0
repeat(6)	C	X	X
		0	6	X
repeat(4)	C	X	X	#CMA instruction at address 6
		0	7	X
repeat(5)	C	X	X	#Indirect BUN instruction at address 7
		0	1	X
repeat(4)	C	X	X	#Indirect BUN instruction at address 7
		0	2	0x0000	#
*/

/* Test case ION:
		CLK	PC	AR	IR	AC	IEN
init S=1;
program(0xF080)
init IEN=0;

		0	0	X	X	X	0
repeat(4)	C	X	X	X	X	X
		0	1	X	X	X	1
*/

/* Test case SPA-NoSkip:
		CLK	AC	PC

init S=1;		#Start computer
init AC=0xF000;		#Prepare AC

program(0x7010, 0x7200, 0x7010, 0x7200)	#SPA CMA SPA CMA

		0	0xF000	0
repeat(4) 	C	X	X
		0	0xF000	1
repeat(4) 	C	X	X
		0	0x0FFF	2
*/

/* Test case IOF:
		CLK	PC	AR	IR	AC	IEN
init S=1;
program(0xF040)
init IEN=1;

		0	0	X	X	X	1
repeat(4)	C	X	X	X	X	X
		0	1	X	X	X	0
*/

/* Test case ISZ_DIRECT-SKIP:
		CLK	PC	DR	AC

init S=1;	#Start computer
init AC=1;

#	0	1	2	3	4	5	6	7
program(0x6005, 0x7020, 0x7200, 0x000,	0x0000, 0xFFFF, 0x7200, 0xC005 ) #Save PC to address 5 and continue execution from 6, then indirect return instruction at 7.

		0	0	X	X
repeat(7)	C	X	X	X
		0	2	X	X
repeat(4)	C	X	X	X
		0	X	X	0xFFFE
*/

/* Test case ISZ_INDIRECT-SKIP:
		CLK	PC	DR	AC

init S=1;	#Start computer
init AC=1;

#	0	1	2	3	4	5	6	7
program(0xE003, 0x7020, 0x7200, 0x0005,	0x0000, 0xFFFF, 0x7200, 0xC005 )

		0	0	X	X
repeat(7)	C	X	X	X
		0	2	X	X
repeat(4)	C	X	X	X
		0	3	X	0xFFFE
*/

/* Test case SNA-Skip:
		CLK	AC	PC

init S=1;		#Start computer
init AC=0xF0F0;		#Prepare AC

program(0x7008, 0x7200)	#SNA CMA

		0	0xF0F0	0
repeat(4) 	C	X	X
		0	0xF0F0	2
*/

/* Test case ISZ_DIRECT-NOSKIP:
		CLK	PC	DR	AC

init S=1;	#Start computer
init AC=1;

#	0	1	2	3	4	5	6	7
program(0x6005, 0x7020, 0x7200, 0x0000,	0x0000, 0x0000, 0x7200, 0xC005 ) #Save PC to address 5 and continue execution from 6, then indirect return instruction at 7.

		0	0	X	X
repeat(7)	C	X	X	X
		0	1	X	X
repeat(4)	C	X	X	X #No skip, and the INC instruction at address 1 is executed
		0	X	X	2
*/

/* Test case ISZ_INDIRECT-NOSKIP:
		CLK	PC	DR	AC

init S=1;	#Start computer
init AC=1;

#	0	1	2	3	4	5	6	7
program(0xE003, 0x7020, 0x7200, 0x0005,	0x0000, 0x0001)

		0	0	X	X
repeat(7)	C	X	X	X
		0	1	X	X
repeat(4)	C	X	X	X #No skip, and the INC instruction at address 1 is executed
		0	X	X	2
*/

/* Test case SNA-NoSkip:
		CLK	AC	PC

init S=1;		#Start computer
init AC=0x0F0F;		#Prepare AC

program(0x7008, 0x7200)	#SNA CMA

		0	0x0F0F	0
repeat(4) 	C	X	X
		0	0x0F0F	1
repeat(4) 	C	X	X
		0	0xF0F0	2
*/

/* Test case SZA-Skip:
		CLK	AC	PC

init S=1;		#Start computer
init AC=0;		#Prepare AC

program(0x7004, 0x7200)	#SNA CMA

		0	0	0
repeat(4) 	C	X	X
		0	0	2
*/

/* Test case SZA-NoSkip:
		CLK	AC	PC

init S=1;		#Start computer
init AC=1;		#Prepare AC

program(0x7004, 0x7200)	#SNA CMA

		0	1	0
repeat(4) 	C	X	X
		0	1	1
repeat(4) 	C	X	X
		0	0xfffe	2
*/

/* Test case SZE-Skip:
		CLK	E	PC

init S=1;		#Start computer
init E=0;		#Prepare AC

program(0x7002, 0x7200)	#SZE CMA

		0	0	0
repeat(4) 	C	X	X
		0	X	2
*/

/* Test case SZE-NoSkip:
		CLK	E	PC	AC

init S=1;		#Start computer
init E=1;		#Prepare E
init AC=0;

program(0x7002, 0x7200)	#SZE CMA

		0	1	0	0
repeat(4) 	C	X	X	X
		0	X	1	0
repeat(4) 	C	X	X	X
		0	X	2	0xFFFF
*/

/* Test case HLT:
		CLK	S	PC	AC

init S=1;	#Start computer
init AC=0;
program(0x7001, 0x7200)	#HLT CMA
	
		0	1	0	0
repeat(4)	C	X	X	X
		0	0	1	0
repeat(4)	C	X	X	X
		0	0	1	0
*/
